# Fritzing sketch loudness_monitor_nano (saved by Fritzing 0.9.4)
circuit board: 6cm x 4cm
perfboards: 1

parts:
  Nano = Arduino Nano (Rev3.0)
  R_Res = Resistor [tolerance=±5% resistance=220 package=THT]
  B_Res = Resistor [tolerance=±5% resistance=220 package=THT]
  G_Res = Resistor [tolerance=±5% resistance=220 package=THT]
  Btn_Res = Resistor [tolerance=±5% resistance=220 package=THT]
  Microphone = Adafruit MAX9814 Electret Microphone Amplifier [part_number="Adafruit #1713"]
  Button = Pushbutton [package="[THT]"]
  RGB_LED = RGB LED (com. cathode, rbg) [package="5 mm [THT]"]

nets:
  GND: Nano.GND, Btn_Res.Pin_0, Microphone.GND
  N1: Nano.D2, Btn_Res.Pin_1, Button.Pin_3, Button.Pin_4
  N2: Nano.D9, B_Res.Pin_0
  N3: Nano.D10, G_Res.Pin_0
  N4: Nano.D11/MOSI, R_Res.Pin_0
  5V: Nano.5V, Microphone.VDD, Microphone.GAIN, Button.Pin_1, Button.Pin_2, RGB_LED.common_cathode
  N5: Nano.A0, Microphone.OUTPUT

custom parts:
  Adafruit MAX9814 Electret Microphone Amplifier: Add an ear to your project with this well-designed electret microphone amplifier with AGC. This fully assembled and tested board comes with a 20-20KHz electret microphone soldered on. For the amplification, we use the Maxim MAX9814, a specialty chip that is designed for amplifying electret microphones in situations where the loudness of the audio isn't predictable. This fancy microphone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
